# Fritzing sketch Turret_Hardware (saved by Fritzing 0.9.3b)
breadboards: 1

parts:
  C1 = Electrolytic Capacitor [capacitance=100μF package="0807 [SMD, electrolytic]"]
  U1 = BUTTONPAD-4X4 [package=buttonpad-4x4]
  Raspberry_Pi_1 = Raspberry Pi 3 [part_number=RPI-3-V1.2]
  LED1 = LED - 3mm [color="Red (633nm)" package="3 mm [THT]"]
  R1 = Resistor [tolerance=±5% resistance=220 package="0402 [SMD]"]
  Part1 = Arduino Mega 2560 (Rev3)
  U2 = LCD-16X2 [package=lcd-16x2]  # not connected
  VCC1 = 4 x AAA Battery Mount  # not connected
  J2 = Basic Servo  # not connected
  U3 = TCM8240MD [package=tcm8240md]  # not connected
  Part2 = Arduino Mega 2560 (Rev3)
  J1 = Basic Servo  # not connected

nets:
  N1: C1.-, R1.Pin_0
  N2: U1.G$5_GRN, Part2.D39
  N3: U1.G$6_RED, Part2.D41
  N4: U1.G$6_GND, Part2.D43
  N5: U1.G$3_SIG1, Part2.D45
  N6: U1.G$6_BLU, Part2.D47
  N7: U1.G$7_RED, Part2.D49
  N8: U1.G$7_GND, Part2.D51
  N9: U1.G$7_BLU, Part2.D53
  N10: Raspberry_Pi_1.GPIO2, Part1.D20/SDA
  N11: Raspberry_Pi_1.GPIO3, Part1.D21/SCL
  N12: LED1.anode, R1.Pin_1

notes:
  CSI BUS
